# Fritzing sketch Pinball Inputs (saved by Fritzing 0.7.9b)
breadboards: 1

parts:
  U20 = IC, DIP package, 14 pins [chip_label=LM339]
  S18 = Resistor [tolerance=±5% resistance=10k package=THT]
  S26 = Resistor [tolerance=±5% resistance=10k package=THT]
  S17 = Resistor [tolerance=±5% resistance=10k package=THT]
  S25 = Resistor [tolerance=±5% resistance=10k package=THT]
  S37 = Resistor [tolerance=±5% resistance=4.7k package=THT]
  S36 = Resistor [tolerance=±5% resistance=4.7k package=THT]
  S35 = Resistor [tolerance=±5% resistance=4.7k package=THT]
  S34 = Resistor [tolerance=±5% resistance=4.7k package=THT]
  R18 = Resistor [tolerance=±5% resistance=10k package=THT]
  R19 = Resistor [tolerance=±5% resistance=4.7k package=THT]
  R27 = Resistor [tolerance=±5% resistance=4.7k package=THT]
  R26 = Resistor [tolerance=±5% resistance=4.7k package=THT]
  R25 = Resistor [tolerance=±5% resistance=4.7k package=THT]
  R24 = Resistor [tolerance=±5% resistance=4.7k package=THT]
  S13 = Resistor [tolerance=±5% resistance=10k package=THT]
  S15 = Resistor [tolerance=±5% resistance=10k package=THT]
  S16 = Resistor [tolerance=±5% resistance=10k package=THT]
  S32 = Resistor [tolerance=±5% resistance=4.7k package=THT]
  S33 = Resistor [tolerance=±5% resistance=4.7k package=THT]
  S38 = Resistor [tolerance=±5% resistance=4.7k package=THT]
  S39 = Resistor [tolerance=±5% resistance=4.7k package=THT]
  R20 = Resistor [tolerance=±5% resistance=4.7k package=THT]
  R21 = Resistor [tolerance=±5% resistance=4.7k package=THT]
  R23 = Resistor [tolerance=±5% resistance=4.7k package=THT]
  R22 = Resistor [tolerance=±5% resistance=4.7k package=THT]
  S24 = Resistor [tolerance=±5% resistance=10k package=THT]
  S25_2 = Resistor [tolerance=±5% resistance=10k package=THT]
  S12 = Resistor [tolerance=±5% resistance=10k package=THT]
  R17 = Resistor [tolerance=±5% resistance=3.3k package=THT]
  R15 = Resistor [tolerance=±5% resistance=3.3k package=THT]
  R16 = Resistor [tolerance=±5% resistance=3.3k package=THT]
  R13 = Resistor [tolerance=±5% resistance=2.2k package=THT]
  R12 = Resistor [tolerance=±5% resistance=2.2k package=THT]
  R14 = Resistor [tolerance=±5% resistance=2.2k package=THT]
  D4 = Rectifier Diode [part_number=1N414B package="300 mil [THT]"]
  D3 = Rectifier Diode [part_number=1N414B package="300 mil [THT]"]
  C39 = Ceramic Capacitor [capacitance=10nF voltage=50V package="100 mil [THT, multilayer]"]
  C37 = Ceramic Capacitor [capacitance=10nF voltage=50V package="100 mil [THT, multilayer]"]
  C35 = Ceramic Capacitor [capacitance=10nF voltage=50V package="100 mil [THT, multilayer]"]
  C34 = Ceramic Capacitor [capacitance=10nF voltage=50V package="100 mil [THT, multilayer]"]
  C36 = Ceramic Capacitor [capacitance=10nF voltage=50V package="100 mil [THT, multilayer]"]
  C33 = Ceramic Capacitor [capacitance=10nF voltage=50V package="100 mil [THT, multilayer]"]
  C32 = Ceramic Capacitor [capacitance=10nF voltage=50V package="100 mil [THT, multilayer]"]
  C31 = Ceramic Capacitor [capacitance=10nF voltage=50V package="100 mil [THT, multilayer]"]
  C30 = Ceramic Capacitor [capacitance=10nF voltage=50V package="100 mil [THT, multilayer]"]
  C26 = Ceramic Capacitor [capacitance=10nF voltage=50V package="100 mil [THT, multilayer]"]
  C25 = Ceramic Capacitor [capacitance=10nF voltage=50V package="100 mil [THT, multilayer]"]
  C27 = Ceramic Capacitor [capacitance=10nF voltage=50V package="100 mil [THT, multilayer]"]
  U21 = IC, DIP package, 14 pins [chip_label=LM339]
  U19 = IC, DIP package, 14 pins [chip_label=LM339]
  SLM_TLT_TST = female pin header, 3 pins [form="♀ (female)"]
  +5VDC = female pin header, 2 pins [form="♀ (female)"]
  RET7-RET4 = female pin header, 4 pins [form="♀ (female)"]
  RET3-RET0 = female pin header, 4 pins [form="♀ (female)"]
  S14 = Resistor [tolerance=±5% resistance=10k package=THT]
  D5 = Rectifier Diode [part_number=1N4001 breakdown_voltage=3.6V package="300 mil [THT]"]
  Pad1 = Pad [width=4.5 height=4.5 connect=center]  # not connected
  part = LED Matrix - Serial Interface - Red/Green/Blue  # not connected
  part_2 = Arduino Xbee Libellium Shield  # not connected
  U22 = Arduino Mega
  part_3 = shrouded pin header, 10 pins [form="♂ (shrouded male)"]  # not connected
  J1 = shrouded pin header, 14 pins [form="♂ (shrouded male)"]
  part_4 = female pin header, 2 pins [form="♀ (female)"]  # not connected
  part_5 = shrouded pin header, 10 pins [form="♂ (shrouded male)"]  # not connected
  J3 = shrouded pin header, 18 pins [form="♂ (shrouded male)"]
  J2 = shrouded pin header, 20 pins [form="♂ (shrouded male)"]

nets:
  N1: U20.pin1, S17.Pin_1, RET7-RET4.pin1, U22.D34
  N2: U20.pin2, S18.Pin_1, RET7-RET4.pin2, U22.D36
  N3: U20.pin3, S18.Pin_0, S26.Pin_0, S17.Pin_0, S25.Pin_0, R18.Pin_0, S13.Pin_0, S15.Pin_0, S16.Pin_0, S24.Pin_0, S25_2.Pin_0, S12.Pin_0, R13.Pin_0, R12.Pin_0, R14.Pin_0, U21.pin3, U19.pin3, +5VDC.pin1, S14.Pin_0
  N4: U20.pin4, S37.Pin_1, R25.Pin_1, C35.1
  N5: U20.pin5, U20.pin7, U20.pin9, U20.pin11, R18.Pin_1, R19.Pin_1, C39.0, U21.pin5, U21.pin7, U21.pin9, U19.pin5, U19.pin7, U19.pin9, U19.pin11
  N6: U20.pin6, S36.Pin_1, R24.Pin_1, C34.1
  N7: U20.pin8, S35.Pin_1, R26.Pin_1, C36.0
  N8: U20.pin10, S34.Pin_1, R27.Pin_1, C37.0
  N9: U20.pin12, S37.Pin_0, S36.Pin_0, S35.Pin_0, S34.Pin_0, R19.Pin_0, S32.Pin_0, S33.Pin_0, S38.Pin_0, S39.Pin_0, C39.1, C37.1, C35.0, C34.0, C36.1, C33.1, C32.1, C31.0, C30.0, C26.0, C25.0, C27.1, U21.pin12, U19.pin12, +5VDC.pin2
  N10: U20.pin13, S25.Pin_1, RET7-RET4.pin4, U22.D40
  N11: U20.pin14, S26.Pin_1, RET7-RET4.pin3, U22.D38
  N12: S13.Pin_1, U19.pin1, RET3-RET0.pin1, U22.D26
  N13: S15.Pin_1, U19.pin14, RET3-RET0.pin3, U22.D30
  N14: S16.Pin_1, U19.pin13, RET3-RET0.pin4, U22.D32
  N15: S32.Pin_1, R21.Pin_1, C30.1, U19.pin4
  N16: S33.Pin_1, R20.Pin_1, C31.1, U19.pin6
  N17: S38.Pin_1, R23.Pin_1, C33.0, U19.pin10
  N18: S39.Pin_1, R22.Pin_1, C32.0, U19.pin8
  N19: S24.Pin_1, U21.pin1, SLM_TLT_TST.pin1, U22.D16
  N20: S25_2.Pin_1, U21.pin2, SLM_TLT_TST.pin2, U22.D15
  N21: S12.Pin_1, U21.pin14, SLM_TLT_TST.pin3, U22.D14
  N22: R17.Pin_0, R14.Pin_1, C27.0, D5.anode
  N23: R17.Pin_1, U21.pin8
  N24: R15.Pin_0, R12.Pin_1, D3.anode, C25.1
  N25: R15.Pin_1, U21.pin6
  N26: R16.Pin_0, R13.Pin_1, D4.anode, C26.1
  N27: R16.Pin_1, U21.pin4
  N28: U19.pin2, RET3-RET0.pin2, S14.Pin_1, U22.D28
  N29: U22.D13, J3.pin13
  N30: U22.D12, J3.pin8
  N31: U22.D11, J3.pin12
  N32: U22.D10, J3.pin7
  N33: U22.D9, J3.pin18
  N34: U22.D8, J3.pin2
  N35: U22.D7, J3.pin17
  N36: U22.D6, J3.pin3
  N37: U22.D5, J3.pin16
  N38: U22.D4, J3.pin4
  N39: U22.D3, J3.pin15
  N40: U22.D2, J3.pin5
  N41: U22.+5V, J3.pin9, J2.pin10
  N42: U22.GND, J1.pin8, J1.pin9, J1.pin10, J1.pin11, J1.pin12, J1.pin13, J1.pin14, J3.pin10, J3.pin11, J2.pin11
  N43: U22.D17, J3.pin1, J2.pin15
  N44: U22.D18, J3.pin14
  N45: U22.D19, J3.pin6
  N46: U22.D22, J2.pin7
  N47: U22.D23, J2.pin14
  N48: U22.D24, J2.pin8
  N49: U22.D25, J2.pin13
  N50: U22.D27, J2.pin6
  N51: U22.D29, J2.pin16
  N52: U22.D31, J2.pin5
  N53: U22.D33, J2.pin17
  N54: U22.D35, J2.pin4
  N55: U22.D37, J2.pin18
  N56: U22.D39, J2.pin3
  N57: U22.D41, J2.pin19
  N58: U22.D42, J2.pin1
  N59: U22.D43, J2.pin20
  N60: U22.D44, J2.pin2
  N61: U22.D45, J2.pin9
  N62: U22.D46, J1.pin1
  N63: U22.D47, J1.pin2
  N64: U22.D48, J1.pin3
  N65: U22.D49, J1.pin4
  N66: U22.D51, J1.pin5
  N67: U22.D53, J1.pin6
